// Logisim project 26_bit_ALU.circ as structural Verilog: 11 circuits, main circuit main
module main (
  input  [1:0] Control,
  input  [25:0] A,
  input  [25:0] B,
  output [25:0] Result,
  output Zero,
  output Negative,
  output Overflow,
  output Carry
);

  L_26_bit_ALU_d6648701 l_26_bit_alu_d6648701_1 (
    .A(A), .B(B), .Control0(Control[0]), .Control1(Control[1]), .Result(Result), .Zero(Zero),
    .Negative(Negative), .Overflow(Overflow), .Carry(Carry));
endmodule

// 26-bit AND
module L_26_bit_and_cc7ceb09 (
  input  [25:0] A,
  input  [25:0] B,
  output [25:0] Result
);

  and and_1 (Result[0], A[0], B[0]);
  and and_2 (Result[1], A[1], B[1]);
  and and_3 (Result[2], A[2], B[2]);
  and and_4 (Result[3], A[3], B[3]);
  and and_5 (Result[4], A[4], B[4]);
  and and_6 (Result[5], A[5], B[5]);
  and and_7 (Result[6], A[6], B[6]);
  and and_8 (Result[7], A[7], B[7]);
  and and_9 (Result[8], A[8], B[8]);
  and and_10 (Result[9], A[9], B[9]);
  and and_11 (Result[10], A[10], B[10]);
  and and_12 (Result[11], A[11], B[11]);
  and and_13 (Result[12], A[12], B[12]);
  and and_14 (Result[13], A[13], B[13]);
  and and_15 (Result[14], A[14], B[14]);
  and and_16 (Result[15], A[15], B[15]);
  and and_17 (Result[16], A[16], B[16]);
  and and_18 (Result[17], A[17], B[17]);
  and and_19 (Result[18], A[18], B[18]);
  and and_20 (Result[19], A[19], B[19]);
  and and_21 (Result[20], A[20], B[20]);
  and and_22 (Result[21], A[21], B[21]);
  and and_23 (Result[22], A[22], B[22]);
  and and_24 (Result[23], A[23], B[23]);
  and and_25 (Result[24], A[24], B[24]);
  and and_26 (Result[25], A[25], B[25]);
endmodule

// 26-bit OR
module L_26_bit_OR_9519f13d (
  input  [25:0] A,
  input  [25:0] B,
  output [25:0] Result
);

  or or_1 (Result[0], A[0], B[0]);
  or or_2 (Result[1], A[1], B[1]);
  or or_3 (Result[2], A[2], B[2]);
  or or_4 (Result[3], A[3], B[3]);
  or or_5 (Result[4], A[4], B[4]);
  or or_6 (Result[5], A[5], B[5]);
  or or_7 (Result[6], A[6], B[6]);
  or or_8 (Result[7], A[7], B[7]);
  or or_9 (Result[8], A[8], B[8]);
  or or_10 (Result[9], A[9], B[9]);
  or or_11 (Result[10], A[10], B[10]);
  or or_12 (Result[11], A[11], B[11]);
  or or_13 (Result[12], A[12], B[12]);
  or or_14 (Result[13], A[13], B[13]);
  or or_15 (Result[14], A[14], B[14]);
  or or_16 (Result[15], A[15], B[15]);
  or or_17 (Result[16], A[16], B[16]);
  or or_18 (Result[17], A[17], B[17]);
  or or_19 (Result[18], A[18], B[18]);
  or or_20 (Result[19], A[19], B[19]);
  or or_21 (Result[20], A[20], B[20]);
  or or_22 (Result[21], A[21], B[21]);
  or or_23 (Result[22], A[22], B[22]);
  or or_24 (Result[23], A[23], B[23]);
  or or_25 (Result[24], A[24], B[24]);
  or or_26 (Result[25], A[25], B[25]);
endmodule

module Full_adder (
  input  Carry_in_9b28b3a3,
  input  A,
  input  B,
  output Result,
  output Carry_out_66355b08
);

  wire and_1_out, and_2_out, xor_1_out;

  and and_1 (and_1_out, B, A);
  xor xor_1 (xor_1_out, A, B);
  or or_1 (Carry_out_66355b08, and_1_out, and_2_out);
  and and_2 (and_2_out, xor_1_out, Carry_in_9b28b3a3);
  xor xor_2 (Result, Carry_in_9b28b3a3, xor_1_out);
endmodule

module L_26_bit_full_adder_66f06b08 (
  input  Carry_in_9b28b3a3,
  input  A0,
  input  B0,
  input  A1,
  input  B1,
  input  A2,
  input  B2,
  input  A3,
  input  B3,
  input  A4,
  input  B4,
  input  A5,
  input  B5,
  input  A6,
  input  B6,
  input  A7,
  input  B7,
  input  A8,
  input  B8,
  input  A9,
  input  B9,
  input  A10,
  input  B10,
  input  A11,
  input  B11,
  input  A12,
  input  B12,
  input  A13,
  input  B13,
  input  A14,
  input  B14,
  input  A15,
  input  B15,
  input  A16,
  input  B16,
  input  A17,
  input  B17,
  input  A18,
  input  B18,
  input  A19,
  input  B19,
  input  A20,
  input  B20,
  input  A21,
  input  B21,
  input  A22,
  input  B22,
  input  A23,
  input  B23,
  input  A24,
  input  B24,
  input  A25,
  input  B25,
  output Result0,
  output Result1,
  output Result2,
  output Result3,
  output Result4,
  output Result5,
  output Result6,
  output Result7,
  output Result8,
  output Result9,
  output Result10,
  output Result11,
  output Result12,
  output Result13,
  output Result14,
  output Result15,
  output Result16,
  output Result17,
  output Result18,
  output Result19,
  output Result20,
  output Result21,
  output Result22,
  output Result23,
  output Result24,
  output Result25,
  output Carry
);

  wire full_adder_1_carry_out_66355b08, full_adder_2_carry_out_66355b08, full_adder_3_carry_out_66355b08,
       full_adder_4_carry_out_66355b08, full_adder_5_carry_out_66355b08, full_adder_6_carry_out_66355b08,
       full_adder_7_carry_out_66355b08, full_adder_8_carry_out_66355b08, full_adder_9_carry_out_66355b08,
       full_adder_10_carry_out_66355b08, full_adder_11_carry_out_66355b08, full_adder_12_carry_out_66355b08,
       full_adder_13_carry_out_66355b08, full_adder_14_carry_out_66355b08, full_adder_15_carry_out_66355b08,
       full_adder_16_carry_out_66355b08, full_adder_17_carry_out_66355b08, full_adder_18_carry_out_66355b08,
       full_adder_19_carry_out_66355b08, full_adder_20_carry_out_66355b08, full_adder_21_carry_out_66355b08,
       full_adder_22_carry_out_66355b08, full_adder_23_carry_out_66355b08, full_adder_24_carry_out_66355b08,
       full_adder_25_carry_out_66355b08;

  Full_adder full_adder_1 (
    .A(A0), .B(B0), .Carry_in_9b28b3a3(Carry_in_9b28b3a3),
    .Carry_out_66355b08(full_adder_1_carry_out_66355b08), .Result(Result0));
  Full_adder full_adder_2 (
    .A(A1), .B(B1), .Carry_in_9b28b3a3(full_adder_1_carry_out_66355b08),
    .Carry_out_66355b08(full_adder_2_carry_out_66355b08), .Result(Result1));
  Full_adder full_adder_3 (
    .A(A2), .B(B2), .Carry_in_9b28b3a3(full_adder_2_carry_out_66355b08),
    .Carry_out_66355b08(full_adder_3_carry_out_66355b08), .Result(Result2));
  Full_adder full_adder_4 (
    .A(A3), .B(B3), .Carry_in_9b28b3a3(full_adder_3_carry_out_66355b08),
    .Carry_out_66355b08(full_adder_4_carry_out_66355b08), .Result(Result3));
  Full_adder full_adder_5 (
    .A(A4), .B(B4), .Carry_in_9b28b3a3(full_adder_4_carry_out_66355b08),
    .Carry_out_66355b08(full_adder_5_carry_out_66355b08), .Result(Result4));
  Full_adder full_adder_6 (
    .A(A5), .B(B5), .Carry_in_9b28b3a3(full_adder_5_carry_out_66355b08),
    .Carry_out_66355b08(full_adder_6_carry_out_66355b08), .Result(Result5));
  Full_adder full_adder_7 (
    .A(A6), .B(B6), .Carry_in_9b28b3a3(full_adder_6_carry_out_66355b08),
    .Carry_out_66355b08(full_adder_7_carry_out_66355b08), .Result(Result6));
  Full_adder full_adder_8 (
    .A(A7), .B(B7), .Carry_in_9b28b3a3(full_adder_7_carry_out_66355b08),
    .Carry_out_66355b08(full_adder_8_carry_out_66355b08), .Result(Result7));
  Full_adder full_adder_9 (
    .A(A8), .B(B8), .Carry_in_9b28b3a3(full_adder_8_carry_out_66355b08),
    .Carry_out_66355b08(full_adder_9_carry_out_66355b08), .Result(Result8));
  Full_adder full_adder_10 (
    .A(A9), .B(B9), .Carry_in_9b28b3a3(full_adder_9_carry_out_66355b08),
    .Carry_out_66355b08(full_adder_10_carry_out_66355b08), .Result(Result9));
  Full_adder full_adder_11 (
    .A(A10), .B(B10), .Carry_in_9b28b3a3(full_adder_10_carry_out_66355b08),
    .Carry_out_66355b08(full_adder_11_carry_out_66355b08), .Result(Result10));
  Full_adder full_adder_12 (
    .A(A11), .B(B11), .Carry_in_9b28b3a3(full_adder_11_carry_out_66355b08),
    .Carry_out_66355b08(full_adder_12_carry_out_66355b08), .Result(Result11));
  Full_adder full_adder_13 (
    .A(A12), .B(B12), .Carry_in_9b28b3a3(full_adder_12_carry_out_66355b08),
    .Carry_out_66355b08(full_adder_13_carry_out_66355b08), .Result(Result12));
  Full_adder full_adder_14 (
    .A(A13), .B(B13), .Carry_in_9b28b3a3(full_adder_13_carry_out_66355b08),
    .Carry_out_66355b08(full_adder_14_carry_out_66355b08), .Result(Result13));
  Full_adder full_adder_15 (
    .A(A14), .B(B14), .Carry_in_9b28b3a3(full_adder_14_carry_out_66355b08),
    .Carry_out_66355b08(full_adder_15_carry_out_66355b08), .Result(Result14));
  Full_adder full_adder_16 (
    .A(A15), .B(B15), .Carry_in_9b28b3a3(full_adder_15_carry_out_66355b08),
    .Carry_out_66355b08(full_adder_16_carry_out_66355b08), .Result(Result15));
  Full_adder full_adder_17 (
    .A(A16), .B(B16), .Carry_in_9b28b3a3(full_adder_16_carry_out_66355b08),
    .Carry_out_66355b08(full_adder_17_carry_out_66355b08), .Result(Result16));
  Full_adder full_adder_18 (
    .A(A17), .B(B17), .Carry_in_9b28b3a3(full_adder_17_carry_out_66355b08),
    .Carry_out_66355b08(full_adder_18_carry_out_66355b08), .Result(Result17));
  Full_adder full_adder_19 (
    .A(A18), .B(B18), .Carry_in_9b28b3a3(full_adder_18_carry_out_66355b08),
    .Carry_out_66355b08(full_adder_19_carry_out_66355b08), .Result(Result18));
  Full_adder full_adder_20 (
    .A(A19), .B(B19), .Carry_in_9b28b3a3(full_adder_19_carry_out_66355b08),
    .Carry_out_66355b08(full_adder_20_carry_out_66355b08), .Result(Result19));
  Full_adder full_adder_21 (
    .A(A20), .B(B20), .Carry_in_9b28b3a3(full_adder_20_carry_out_66355b08),
    .Carry_out_66355b08(full_adder_21_carry_out_66355b08), .Result(Result20));
  Full_adder full_adder_22 (
    .A(A21), .B(B21), .Carry_in_9b28b3a3(full_adder_21_carry_out_66355b08),
    .Carry_out_66355b08(full_adder_22_carry_out_66355b08), .Result(Result21));
  Full_adder full_adder_23 (
    .A(A22), .B(B22), .Carry_in_9b28b3a3(full_adder_22_carry_out_66355b08),
    .Carry_out_66355b08(full_adder_23_carry_out_66355b08), .Result(Result22));
  Full_adder full_adder_24 (
    .A(A23), .B(B23), .Carry_in_9b28b3a3(full_adder_23_carry_out_66355b08),
    .Carry_out_66355b08(full_adder_24_carry_out_66355b08), .Result(Result23));
  Full_adder full_adder_25 (
    .A(A24), .B(B24), .Carry_in_9b28b3a3(full_adder_24_carry_out_66355b08),
    .Carry_out_66355b08(full_adder_25_carry_out_66355b08), .Result(Result24));
  Full_adder full_adder_26 (
    .A(A25), .B(B25), .Carry_in_9b28b3a3(full_adder_25_carry_out_66355b08), .Carry_out_66355b08(Carry),
    .Result(Result25));
endmodule

// FA
module L_26_bit_full_adder_concise_0d2034b4 (
  input  Carry_in_9b28b3a3,
  input  [25:0] A,
  input  [25:0] B,
  output [25:0] Result,
  output Carry
);

  wire full_adder_1_carry_out_66355b08, full_adder_2_carry_out_66355b08, full_adder_3_carry_out_66355b08,
       full_adder_4_carry_out_66355b08, full_adder_5_carry_out_66355b08, full_adder_6_carry_out_66355b08,
       full_adder_7_carry_out_66355b08, full_adder_8_carry_out_66355b08, full_adder_9_carry_out_66355b08,
       full_adder_10_carry_out_66355b08, full_adder_11_carry_out_66355b08, full_adder_12_carry_out_66355b08,
       full_adder_13_carry_out_66355b08, full_adder_14_carry_out_66355b08, full_adder_15_carry_out_66355b08,
       full_adder_16_carry_out_66355b08, full_adder_17_carry_out_66355b08, full_adder_18_carry_out_66355b08,
       full_adder_19_carry_out_66355b08, full_adder_20_carry_out_66355b08, full_adder_21_carry_out_66355b08,
       full_adder_22_carry_out_66355b08, full_adder_23_carry_out_66355b08, full_adder_24_carry_out_66355b08,
       full_adder_25_carry_out_66355b08;

  Full_adder full_adder_1 (
    .A(A[0]), .B(B[0]), .Carry_in_9b28b3a3(Carry_in_9b28b3a3),
    .Carry_out_66355b08(full_adder_1_carry_out_66355b08), .Result(Result[0]));
  Full_adder full_adder_2 (
    .A(A[1]), .B(B[1]), .Carry_in_9b28b3a3(full_adder_1_carry_out_66355b08),
    .Carry_out_66355b08(full_adder_2_carry_out_66355b08), .Result(Result[1]));
  Full_adder full_adder_3 (
    .A(A[2]), .B(B[2]), .Carry_in_9b28b3a3(full_adder_2_carry_out_66355b08),
    .Carry_out_66355b08(full_adder_3_carry_out_66355b08), .Result(Result[2]));
  Full_adder full_adder_4 (
    .A(A[3]), .B(B[3]), .Carry_in_9b28b3a3(full_adder_3_carry_out_66355b08),
    .Carry_out_66355b08(full_adder_4_carry_out_66355b08), .Result(Result[3]));
  Full_adder full_adder_5 (
    .A(A[4]), .B(B[4]), .Carry_in_9b28b3a3(full_adder_4_carry_out_66355b08),
    .Carry_out_66355b08(full_adder_5_carry_out_66355b08), .Result(Result[4]));
  Full_adder full_adder_6 (
    .A(A[5]), .B(B[5]), .Carry_in_9b28b3a3(full_adder_5_carry_out_66355b08),
    .Carry_out_66355b08(full_adder_6_carry_out_66355b08), .Result(Result[5]));
  Full_adder full_adder_7 (
    .A(A[6]), .B(B[6]), .Carry_in_9b28b3a3(full_adder_6_carry_out_66355b08),
    .Carry_out_66355b08(full_adder_7_carry_out_66355b08), .Result(Result[6]));
  Full_adder full_adder_8 (
    .A(A[7]), .B(B[7]), .Carry_in_9b28b3a3(full_adder_7_carry_out_66355b08),
    .Carry_out_66355b08(full_adder_8_carry_out_66355b08), .Result(Result[7]));
  Full_adder full_adder_9 (
    .A(A[8]), .B(B[8]), .Carry_in_9b28b3a3(full_adder_8_carry_out_66355b08),
    .Carry_out_66355b08(full_adder_9_carry_out_66355b08), .Result(Result[8]));
  Full_adder full_adder_10 (
    .A(A[9]), .B(B[9]), .Carry_in_9b28b3a3(full_adder_9_carry_out_66355b08),
    .Carry_out_66355b08(full_adder_10_carry_out_66355b08), .Result(Result[9]));
  Full_adder full_adder_11 (
    .A(A[10]), .B(B[10]), .Carry_in_9b28b3a3(full_adder_10_carry_out_66355b08),
    .Carry_out_66355b08(full_adder_11_carry_out_66355b08), .Result(Result[10]));
  Full_adder full_adder_12 (
    .A(A[11]), .B(B[11]), .Carry_in_9b28b3a3(full_adder_11_carry_out_66355b08),
    .Carry_out_66355b08(full_adder_12_carry_out_66355b08), .Result(Result[11]));
  Full_adder full_adder_13 (
    .A(A[12]), .B(B[12]), .Carry_in_9b28b3a3(full_adder_12_carry_out_66355b08),
    .Carry_out_66355b08(full_adder_13_carry_out_66355b08), .Result(Result[12]));
  Full_adder full_adder_14 (
    .A(A[13]), .B(B[13]), .Carry_in_9b28b3a3(full_adder_13_carry_out_66355b08),
    .Carry_out_66355b08(full_adder_14_carry_out_66355b08), .Result(Result[13]));
  Full_adder full_adder_15 (
    .A(A[14]), .B(B[14]), .Carry_in_9b28b3a3(full_adder_14_carry_out_66355b08),
    .Carry_out_66355b08(full_adder_15_carry_out_66355b08), .Result(Result[14]));
  Full_adder full_adder_16 (
    .A(A[15]), .B(B[15]), .Carry_in_9b28b3a3(full_adder_15_carry_out_66355b08),
    .Carry_out_66355b08(full_adder_16_carry_out_66355b08), .Result(Result[15]));
  Full_adder full_adder_17 (
    .A(A[16]), .B(B[16]), .Carry_in_9b28b3a3(full_adder_16_carry_out_66355b08),
    .Carry_out_66355b08(full_adder_17_carry_out_66355b08), .Result(Result[16]));
  Full_adder full_adder_18 (
    .A(A[17]), .B(B[17]), .Carry_in_9b28b3a3(full_adder_17_carry_out_66355b08),
    .Carry_out_66355b08(full_adder_18_carry_out_66355b08), .Result(Result[17]));
  Full_adder full_adder_19 (
    .A(A[18]), .B(B[18]), .Carry_in_9b28b3a3(full_adder_18_carry_out_66355b08),
    .Carry_out_66355b08(full_adder_19_carry_out_66355b08), .Result(Result[18]));
  Full_adder full_adder_20 (
    .A(A[19]), .B(B[19]), .Carry_in_9b28b3a3(full_adder_19_carry_out_66355b08),
    .Carry_out_66355b08(full_adder_20_carry_out_66355b08), .Result(Result[19]));
  Full_adder full_adder_21 (
    .A(A[20]), .B(B[20]), .Carry_in_9b28b3a3(full_adder_20_carry_out_66355b08),
    .Carry_out_66355b08(full_adder_21_carry_out_66355b08), .Result(Result[20]));
  Full_adder full_adder_22 (
    .A(A[21]), .B(B[21]), .Carry_in_9b28b3a3(full_adder_21_carry_out_66355b08),
    .Carry_out_66355b08(full_adder_22_carry_out_66355b08), .Result(Result[21]));
  Full_adder full_adder_23 (
    .A(A[22]), .B(B[22]), .Carry_in_9b28b3a3(full_adder_22_carry_out_66355b08),
    .Carry_out_66355b08(full_adder_23_carry_out_66355b08), .Result(Result[22]));
  Full_adder full_adder_24 (
    .A(A[23]), .B(B[23]), .Carry_in_9b28b3a3(full_adder_23_carry_out_66355b08),
    .Carry_out_66355b08(full_adder_24_carry_out_66355b08), .Result(Result[23]));
  Full_adder full_adder_25 (
    .A(A[24]), .B(B[24]), .Carry_in_9b28b3a3(full_adder_24_carry_out_66355b08),
    .Carry_out_66355b08(full_adder_25_carry_out_66355b08), .Result(Result[24]));
  Full_adder full_adder_26 (
    .A(A[25]), .B(B[25]), .Carry_in_9b28b3a3(full_adder_25_carry_out_66355b08), .Carry_out_66355b08(Carry),
    .Result(Result[25]));
endmodule

module L_26_bit_xor_473c1eb2 (
  input  Control,
  input  [25:0] B,
  output [25:0] Result
);

  wire [25:0] bit_extender_1_out;

  assign bit_extender_1_out = {{25{Control}}, Control};  // Bit_Extender bit_extender_1
  assign Result = bit_extender_1_out ^ B;  // XOR_Gate xor_1, 26 bits wide
endmodule

// 26-bit \nADD/SUB
module Add_sub (
  input  Sub,
  input  [25:0] A,
  input  [25:0] B,
  output [25:0] Result,
  output Carry,
  output Overflow
);

  wire and_1_out, and_2_out, l_25th_bit_out_f70d8717_1_l_25th_bit_93b1782c,
       l_25th_bit_out_f70d8717_2_l_25th_bit_93b1782c, l_25th_bit_out_f70d8717_3_l_25th_bit_93b1782c,
       not_1_out, not_2_out, not_3_out;
  wire [25:0] l_26_bit_xor_473c1eb2_1_result;

  L_25th_bit_out_f70d8717 l_25th_bit_out_f70d8717_1 (
    .Input(A), .L_25th_bit_93b1782c(l_25th_bit_out_f70d8717_1_l_25th_bit_93b1782c));
  not not_1 (not_1_out, l_25th_bit_out_f70d8717_1_l_25th_bit_93b1782c);
  L_25th_bit_out_f70d8717 l_25th_bit_out_f70d8717_2 (
    .Input(B), .L_25th_bit_93b1782c(l_25th_bit_out_f70d8717_2_l_25th_bit_93b1782c));
  not not_2 (not_2_out, l_25th_bit_out_f70d8717_2_l_25th_bit_93b1782c);
  L_26_bit_xor_473c1eb2 l_26_bit_xor_473c1eb2_1 (.Control(Sub), .B(B), .Result(l_26_bit_xor_473c1eb2_1_result));
  L_26_bit_full_adder_concise_0d2034b4 l_26_bit_full_adder_concise_0d2034b4_1 (
    .Carry_in_9b28b3a3(Sub), .B(l_26_bit_xor_473c1eb2_1_result), .A(A), .Carry(Carry), .Result(Result));
  L_25th_bit_out_f70d8717 l_25th_bit_out_f70d8717_3 (
    .Input(Result), .L_25th_bit_93b1782c(l_25th_bit_out_f70d8717_3_l_25th_bit_93b1782c));
  not not_3 (not_3_out, l_25th_bit_out_f70d8717_3_l_25th_bit_93b1782c);
  and and_1 (and_1_out, not_3_out, l_25th_bit_out_f70d8717_2_l_25th_bit_93b1782c, l_25th_bit_out_f70d8717_1_l_25th_bit_93b1782c);
  and and_2 (and_2_out, l_25th_bit_out_f70d8717_3_l_25th_bit_93b1782c, not_2_out, not_1_out);
  or or_1 (Overflow, and_1_out, and_2_out);

  // Notes on the sheet:
  //   A31
  //   B31
  //   Result 31
endmodule

// 25th
module L_25th_bit_out_f70d8717 (
  input  [25:0] Input,
  output L_25th_bit_93b1782c
);


  assign L_25th_bit_93b1782c = Input[25];
endmodule

// Reduce-OR
module L_26_bit_reduce_or_5d1646df (
  input  [25:0] Input,
  output Output
);

  or or_1 (Output, Input[0], Input[1], Input[2], Input[3], Input[4], Input[5], Input[6], Input[7], Input[8], Input[9], Input[10], Input[11], Input[12], Input[13], Input[14], Input[15], Input[16], Input[17], Input[18], Input[19], Input[20], Input[21], Input[22], Input[23], Input[24], Input[25]);
endmodule

// 26-bit-ALU
module L_26_bit_ALU_d6648701 (
  input  Control0,
  input  Control1,
  input  [25:0] A,
  input  [25:0] B,
  output [25:0] Result,
  output Zero,
  output Negative,
  output Overflow,
  output Carry
);

  wire l_26_bit_reduce_or_5d1646df_1_output;
  wire [25:0] add_sub_1_result, l_26_bit_and_cc7ceb09_1_result, l_26_bit_or_9519f13d_1_result,
       multiplexer_1_out;

  L_26_bit_and_cc7ceb09 l_26_bit_and_cc7ceb09_1 (.A(A), .B(B), .Result(l_26_bit_and_cc7ceb09_1_result));
  L_26_bit_OR_9519f13d l_26_bit_or_9519f13d_1 (.A(A), .B(B), .Result(l_26_bit_or_9519f13d_1_result));
  Add_sub add_sub_1 (.A(A), .B(B), .Sub(Control0), .Overflow(Overflow), .Carry(Carry), .Result(add_sub_1_result));
  Multiplexer #(.width(26)) multiplexer_1 (
    .in0(l_26_bit_and_cc7ceb09_1_result), .in1(l_26_bit_or_9519f13d_1_result), .out(multiplexer_1_out),
    .sel(Control0));
  Multiplexer #(.width(26)) multiplexer_2 (
    .in0(multiplexer_1_out), .in1(add_sub_1_result), .out(Result), .sel(Control1));
  L_25th_bit_out_f70d8717 l_25th_bit_out_f70d8717_1 (.Input(Result), .L_25th_bit_93b1782c(Negative));
  L_26_bit_reduce_or_5d1646df l_26_bit_reduce_or_5d1646df_1 (
    .Input(Result), .Output(l_26_bit_reduce_or_5d1646df_1_output));
  not not_1 (Zero, l_26_bit_reduce_or_5d1646df_1_output);
endmodule
