// Logisim project Booth's circuit for 26 bit.circ as structural Verilog: 11 circuits, main circuit Booth's multiplier
module Booth_s_multiplier (
  input  [25:0] M_input,
  input  [25:0] Q_input,
  input  Reset
);

  wire A_out, clock_1_out, controller_1_c0, controller_1_c1, controller_1_cl__a__q_1, controller_1_dec_cnt,
       controller_1_load__m__q__cnt, controller_1_load_a, controller_1_shr, or_1_out, Q__1_q0, Q_out, Q_q3;
  wire [2:0] counter_1_q;
  wire [25:0] A_q25, M_q25, n26_bit_alu_1_result;

  Clock clock_1 (.out(clock_1_out));
  Controller controller_1 (
    .Clk(clock_1_out), .Q0(Q_q3), .Q_1(Q__1_q0), .Count(counter_1_q), .C0(controller_1_c0),
    .C1(controller_1_c1), .Shr(controller_1_shr), .Dec_Cnt(controller_1_dec_cnt),
    .Cl__A__Q_1(controller_1_cl__a__q_1), .Load_A(controller_1_load_a),
    .LOad__M__Q__Cnt(controller_1_load__m__q__cnt), .Reset(Reset));
  or or_1 (or_1_out, controller_1_load__m__q__cnt, controller_1_dec_cnt);
  Counter #(.width(3), .max('h4)) counter_1 (
    .load(or_1_out), .D(3'b100), .count(controller_1_dec_cnt), .Q(counter_1_q), .clk(clock_1_out));  // open: carry, clr
  Shift_Register #(.length(26)) A (
    .shift(controller_1_shr), .in(A_q25[25]), .clk(clock_1_out), .out(A_out), .load(controller_1_load_a),
    .clr(controller_1_cl__a__q_1), .d0(n26_bit_alu_1_result[25]), .q0(A_q25[25]),
    .d1(n26_bit_alu_1_result[24]), .q1(A_q25[24]), .d2(n26_bit_alu_1_result[23]), .q2(A_q25[23]),
    .d3(n26_bit_alu_1_result[22]), .q3(A_q25[22]), .d4(n26_bit_alu_1_result[21]), .q4(A_q25[21]),
    .d5(n26_bit_alu_1_result[20]), .q5(A_q25[20]), .d6(n26_bit_alu_1_result[19]), .q6(A_q25[19]),
    .d7(n26_bit_alu_1_result[18]), .q7(A_q25[18]), .d8(n26_bit_alu_1_result[17]), .q8(A_q25[17]),
    .d9(n26_bit_alu_1_result[16]), .q9(A_q25[16]), .d10(n26_bit_alu_1_result[15]), .q10(A_q25[15]),
    .d11(n26_bit_alu_1_result[14]), .q11(A_q25[14]), .d12(n26_bit_alu_1_result[13]), .q12(A_q25[13]),
    .d13(n26_bit_alu_1_result[12]), .q13(A_q25[12]), .d14(n26_bit_alu_1_result[11]), .q14(A_q25[11]),
    .d15(n26_bit_alu_1_result[10]), .q15(A_q25[10]), .d16(n26_bit_alu_1_result[9]), .q16(A_q25[9]),
    .d17(n26_bit_alu_1_result[8]), .q17(A_q25[8]), .d18(n26_bit_alu_1_result[7]), .q18(A_q25[7]),
    .d19(n26_bit_alu_1_result[6]), .q19(A_q25[6]), .d20(n26_bit_alu_1_result[5]), .q20(A_q25[5]),
    .d21(n26_bit_alu_1_result[4]), .q21(A_q25[4]), .d22(n26_bit_alu_1_result[3]), .q22(A_q25[3]),
    .d23(n26_bit_alu_1_result[2]), .q23(A_q25[2]), .d24(n26_bit_alu_1_result[1]), .q24(A_q25[1]),
    .d25(n26_bit_alu_1_result[0]), .q25(A_q25[0]));
  Shift_Register #(.length(26)) M (
    .shift(1'b0), .clk(clock_1_out), .load(controller_1_load__m__q__cnt), .d0(M_input[25]), .q0(M_q25[25]),
    .d1(M_input[24]), .q1(M_q25[24]), .d2(M_input[23]), .q2(M_q25[23]), .d3(M_input[22]), .q3(M_q25[22]),
    .d4(M_input[21]), .q4(M_q25[21]), .d5(M_input[20]), .q5(M_q25[20]), .d6(M_input[19]), .q6(M_q25[19]),
    .d7(M_input[18]), .q7(M_q25[18]), .d8(M_input[17]), .q8(M_q25[17]), .d9(M_input[16]), .q9(M_q25[16]),
    .d10(M_input[15]), .q10(M_q25[15]), .d11(M_input[14]), .q11(M_q25[14]), .d12(M_input[13]),
    .q12(M_q25[13]), .d13(M_input[12]), .q13(M_q25[12]), .d14(M_input[11]), .q14(M_q25[11]),
    .d15(M_input[10]), .q15(M_q25[10]), .d16(M_input[9]), .q16(M_q25[9]), .d17(M_input[8]), .q17(M_q25[8]),
    .d18(M_input[7]), .q18(M_q25[7]), .d19(M_input[6]), .q19(M_q25[6]), .d20(M_input[5]), .q20(M_q25[5]),
    .d21(M_input[4]), .q21(M_q25[4]), .d22(M_input[3]), .q22(M_q25[3]), .d23(M_input[2]), .q23(M_q25[2]),
    .d24(M_input[1]), .q24(M_q25[1]), .d25(M_input[0]), .q25(M_q25[0]));  // open: in, out, clr
  _26_bit_ALU u_26_bit_alu_1 (
    .A(A_q25), .B(M_q25), .Result(n26_bit_alu_1_result), .Control0(controller_1_c1),
    .Control1(controller_1_c0));  // open: Zero, Negative, Overflow, Carry
  Shift_Register #(.length(26)) Q (
    .shift(controller_1_shr), .in(A_out), .clk(clock_1_out), .out(Q_out),
    .load(controller_1_load__m__q__cnt), .d0(Q_input[25]), .d1(Q_input[24]), .d2(Q_input[23]),
    .d3(Q_input[22]), .q3(Q_q3), .d4(Q_input[21]), .d5(Q_input[20]), .d6(Q_input[19]), .d7(Q_input[18]),
    .d8(Q_input[17]), .d9(Q_input[16]), .d10(Q_input[15]), .d11(Q_input[14]), .d12(Q_input[13]),
    .d13(Q_input[12]), .d14(Q_input[11]), .d15(Q_input[10]), .d16(Q_input[9]), .d17(Q_input[8]),
    .d18(Q_input[7]), .d19(Q_input[6]), .d20(Q_input[5]), .d21(Q_input[4]), .d22(Q_input[3]),
    .d23(Q_input[2]), .d24(Q_input[1]), .d25(Q_input[0]));  // open: clr, q0, q1, q2, q4, q5, q6, q7, q8, q9, q10, q11, q12, q13, q14, q15, q16, q17, q18, q19, q20, q21, q22, q23, q24, q25
  Shift_Register #(.length(1)) Q__1 (
    .shift(controller_1_shr), .in(Q_out), .clk(clock_1_out), .clr(controller_1_cl__a__q_1), .q0(Q__1_q0));  // open: out, load, d0
endmodule

// 26-bit AND
module _26_bit_and (
  input  [25:0] A,
  input  [25:0] B,
  output [25:0] Result
);

  assign Result = A & B;  // AND_Gate and_1, 26 bits wide
endmodule

// 26-bit OR
module _26_bit_OR (
  input  [25:0] A,
  input  [25:0] B,
  output [25:0] Result
);

  assign Result = A | B;  // OR_Gate or_1, 26 bits wide
endmodule

module Full_adder (
  input  Carry_in,
  input  A,
  input  B,
  output Result,
  output Carry_out
);

  wire and_1_out, and_2_out, xor_1_out;

  and and_1 (and_1_out, B, A);
  xor xor_1 (xor_1_out, A, B);
  or or_1 (Carry_out, and_1_out, and_2_out);
  and and_2 (and_2_out, xor_1_out, Carry_in);
  xor xor_2 (Result, Carry_in, xor_1_out);
endmodule

module _4_bit_full_adder (
  input  Carry_in,
  input  [3:0] A,
  input  [3:0] B,
  output [3:0] Result,
  output Carry
);

  wire full_adder_1_carry_out, full_adder_2_carry_out, full_adder_3_carry_out;

  Full_adder full_adder_1 (
    .Carry_in(Carry_in), .A(A[0]), .B(B[0]), .Result(Result[0]), .Carry_out(full_adder_1_carry_out));
  Full_adder full_adder_2 (
    .Carry_in(full_adder_1_carry_out), .A(A[1]), .B(B[1]), .Result(Result[1]),
    .Carry_out(full_adder_2_carry_out));
  Full_adder full_adder_3 (
    .Carry_in(full_adder_2_carry_out), .A(A[2]), .B(B[2]), .Result(Result[2]),
    .Carry_out(full_adder_3_carry_out));
  Full_adder full_adder_4 (
    .Carry_in(full_adder_3_carry_out), .A(A[3]), .B(B[3]), .Result(Result[3]), .Carry_out(Carry));
endmodule

module _4_bit_xor (
  input  Control,
  input  [3:0] B,
  output [3:0] Result
);

  wire [3:0] bit_extender_1_out;

  assign bit_extender_1_out = {{3{Control}}, Control};  // Bit_Extender bit_extender_1
  assign Result = bit_extender_1_out ^ B;  // XOR_Gate xor_1, 4 bits wide
endmodule

// 32-bit \nADD/SUB
module Add_sub (
  input  Sub,
  input  [3:0] A,
  input  [3:0] B,
  output [3:0] Result,
  output Carry,
  output Overflow
);

  wire and_1_out, and_2_out, not_1_out, not_2_out, not_3_out, sign_bit_out_1_ms_bit, sign_bit_out_2_ms_bit,
       sign_bit_out_3_ms_bit;
  wire [3:0] n4_bit_xor_1_result;

  sign_bit_out sign_bit_out_1 (.Input(A), .MS_bit(sign_bit_out_1_ms_bit));
  not not_1 (not_1_out, sign_bit_out_1_ms_bit);
  _4_bit_xor u_4_bit_xor_1 (.B(B), .Result(n4_bit_xor_1_result), .Control(Sub));
  sign_bit_out sign_bit_out_2 (.Input(n4_bit_xor_1_result), .MS_bit(sign_bit_out_2_ms_bit));
  not not_2 (not_2_out, sign_bit_out_2_ms_bit);
  _4_bit_full_adder u_4_bit_full_adder_1 (
    .A(A), .B(n4_bit_xor_1_result), .Result(Result), .Carry_in(Sub), .Carry(Carry));
  sign_bit_out sign_bit_out_3 (.Input(Result), .MS_bit(sign_bit_out_3_ms_bit));
  not not_3 (not_3_out, sign_bit_out_3_ms_bit);
  and and_1 (and_1_out, not_3_out, sign_bit_out_2_ms_bit, sign_bit_out_1_ms_bit);
  and and_2 (and_2_out, sign_bit_out_3_ms_bit, not_2_out, not_1_out);
  or or_1 (Overflow, and_1_out, and_2_out);

  // Notes on the sheet:
  //   A31
  //   B31
  //   Result 31
endmodule

// 31th
module sign_bit_out (
  input  [3:0] Input,
  output MS_bit
);


  assign MS_bit = Input[3];
endmodule

// Reduce-OR
module _4_bit_reduce_or (
  input  [3:0] Input,
  output Output
);

  or or_1 (Output, Input[0], Input[1], Input[2], Input[3]);
endmodule

// 4 bit ALU
module _4bit_ALU (
  input  Control0,
  input  Control1,
  input  [3:0] A,
  input  [3:0] B,
  output [3:0] Result,
  output Zero,
  output Negative,
  output Overflow,
  output Carry
);

  wire n4_bit_reduce_or_1_output;
  wire [3:0] add_sub_1_result, multiplexer_1_out, n26_bit_and_1_p3, n26_bit_or_1_p3;

  // _26_bit_and 26_bit_and_1: pin names not known; wires that end beside it: A, B, n26_bit_and_1_p3
  // _26_bit_OR 26_bit_or_1: pin names not known; wires that end beside it: A, B, n26_bit_or_1_p3
  Add_sub add_sub_1 (.Sub(Control0), .A(A), .B(B), .Result(add_sub_1_result), .Carry(Carry), .Overflow(Overflow));
  Multiplexer #(.width(4), .enable("false")) multiplexer_1 (
    .in0(n26_bit_and_1_p3), .in1(n26_bit_or_1_p3), .out(multiplexer_1_out), .sel(Control0));
  Multiplexer #(.width(4), .enable("false")) multiplexer_2 (
    .in0(multiplexer_1_out), .in1(add_sub_1_result), .out(Result), .sel(Control1));
  sign_bit_out sign_bit_out_1 (.Input(Result), .MS_bit(Negative));
  _4_bit_reduce_or u_4_bit_reduce_or_1 (.Input(Result), .Output(n4_bit_reduce_or_1_output));
  not not_1 (Zero, n4_bit_reduce_or_1_output);
endmodule

// Control \nUnit
module Controller (
  input  Clk,
  input  Reset,
  input  Q0,
  input  Q_1,
  input  [2:0] Count,
  output Cl__A__Q_1,
  output LOad__M__Q__Cnt,
  output Load_A,
  output C0,
  output C1,
  output Shr,
  output Dec_Cnt
);

  wire and_3_out, multiplexer_1_out, not_1_out, not_2_out, not_3_out, not_4_out, not_5_out, not_6_out,
       not_7_out, or_2_out, Q0_prime_Q_1_out, Q0Q_1_prime_out;
  wire [1:0] rom_1_data_2;
  wire [2:0] and_1_out, and_2_out, bit_extender_1_out, bit_extender_2_out, bit_extender_3_out, CAR_q,
       or_1_out, rom_1_data;

  assign bit_extender_1_out = {{2{Q0_prime_Q_1_out}}, Q0_prime_Q_1_out};  // Bit_Extender bit_extender_1
  and Q0_prime_Q_1 (Q0_prime_Q_1_out, not_2_out, Q_1);
  not not_1 (not_1_out, Q0_prime_Q_1_out);
  assign bit_extender_2_out = {{2{not_1_out}}, not_1_out};  // Bit_Extender bit_extender_2
  assign and_1_out = 3'b100 & bit_extender_3_out & bit_extender_1_out;  // AND_Gate and_1, 3 bits wide
  assign or_1_out = and_1_out | rom_1_data | and_2_out;  // OR_Gate or_1, 3 bits wide
  not not_2 (not_2_out, Q0);
  assign and_2_out = bit_extender_2_out & bit_extender_3_out & 3'b101;  // AND_Gate and_2, 3 bits wide
  assign bit_extender_3_out = {{2{and_3_out}}, and_3_out};  // Bit_Extender bit_extender_3
  and and_3 (and_3_out, not_4_out, CAR_q[1], not_3_out);
  not not_3 (not_3_out, CAR_q[0]);
  not not_4 (not_4_out, CAR_q[2]);
  Counter #(.width(3), .max('h7)) CAR (
    .load(not_5_out), .D(or_1_out), .count(multiplexer_1_out), .Q(CAR_q), .clk(Clk), .clr(Reset));  // open: carry
  not not_5 (not_5_out, multiplexer_1_out);
  Multiplexer #(.select(2), .enable("false")) multiplexer_1 (
    .in0(1'b0), .in1(1'b1), .in2(Q0Q_1_prime_out), .in3(not_7_out), .out(multiplexer_1_out),
    .sel(rom_1_data_2));
  ROM #(.addrWidth(3), .dataWidth(12)) rom_1 (
    .addr(CAR_q), .data({Cl__A__Q_1, LOad__M__Q__Cnt, Load_A, C0, C1, Shr, Dec_Cnt, rom_1_data, rom_1_data_2}));  // open: sel
  and Q0Q_1_prime (Q0Q_1_prime_out, not_6_out, Q0);
  not not_6 (not_6_out, Q_1);
  or or_2 (or_2_out, Count[0], Count[1], Count[2]);
  not not_7 (not_7_out, or_2_out);

  // Notes on the sheet:
  //   To choose only
  //   state 2 (010)
  //   Control Word Format: Clear (A, Q-1), Load (M, Q, Cnt), Load A, C0, C1, Shr, Dec Cnt, Address bits (3 bit), Selection bits (2 bit)
  //   contents of rom_1 (hex, n*v repeats v):
  //   1 c01 2 394 281 61 b 1c
endmodule
